// Logisim project innovassi.circ as structural Verilog: 1 circuit, main circuit main
module main (
);

  wire and_1_out, and_2_out, and_3_out, and_4_out, and_5_out, and_6_out, and_7_out, and_8_out, and_9_out,
       and_10_out, ASSIGN0_out, ASSIGN1_out, ASSIGN2_out, ASSIGN3_out, ASSIGN4_out, ASSIGN5_out, ASSIGN6_out,
       ASSIGN7_out, ASSIGN8_out, ASSIGN9_out, d_ff_1_q, d_ff_2_q, d_ff_3_q, d_ff_4_q, d_ff_5_q, d_ff_6_q,
       d_ff_7_q, d_ff_8_q, d_ff_9_q, d_ff_9_qn, d_ff_10_q, d_ff_10_qn, d_ff_11_q, d_ff_11_qn, d_ff_12_q,
       d_ff_12_qn, d_ff_13_q, d_ff_13_qn, d_ff_14_q, d_ff_14_qn, d_ff_15_q, d_ff_15_qn, d_ff_16_q,
       d_ff_16_qn, FREE0_out, FREE9_out, not_1_out, not_2_out, not_3_out, not_4_out, not_5_out, not_6_out,
       not_7_out, not_8_out, not_9_out, not_10_out, not_11_out, not_12_out, not_13_out, not_14_out,
       not_15_out, not_16_out, not_17_out, or_1_out, or_2_out, or_3_out, or_4_out, or_5_out, or_6_out,
       or_7_out, or_8_out, or_9_out, REQ_out, Retain_0_q, Retain_0_qn, Retain_9_q, Retain_9_qn, Room_0_q,
       Room_9_q;

  Button REQ (.out(REQ_out));
  and and_1 (and_1_out, REQ_out, ASSIGN9_out);
  and and_2 (and_2_out, REQ_out, ASSIGN8_out);
  and and_3 (and_3_out, REQ_out, ASSIGN7_out);
  and and_4 (and_4_out, REQ_out, ASSIGN6_out);
  and and_5 (and_5_out, REQ_out, ASSIGN5_out);
  and and_6 (and_6_out, REQ_out, ASSIGN4_out);
  and and_7 (and_7_out, REQ_out, ASSIGN3_out);
  and and_8 (and_8_out, REQ_out, ASSIGN2_out);
  and and_9 (and_9_out, REQ_out, ASSIGN1_out);
  and and_10 (and_10_out, REQ_out, ASSIGN0_out);
  D_Flip_Flop Room_9 (.clk(and_1_out), .Q(Room_9_q));  // open: D, Qn, preset, en, reset
  D_Flip_Flop d_ff_1 (.clk(and_2_out), .Q(d_ff_1_q));  // open: D, Qn, preset, en, reset
  D_Flip_Flop d_ff_2 (.clk(and_3_out), .Q(d_ff_2_q));  // open: D, Qn, preset, en, reset
  D_Flip_Flop d_ff_3 (.clk(and_4_out), .Q(d_ff_3_q));  // open: D, Qn, preset, en, reset
  D_Flip_Flop d_ff_4 (.clk(and_5_out), .Q(d_ff_4_q));  // open: D, Qn, preset, en, reset
  D_Flip_Flop d_ff_5 (.clk(and_6_out), .Q(d_ff_5_q));  // open: D, Qn, preset, en, reset
  D_Flip_Flop d_ff_6 (.clk(and_7_out), .Q(d_ff_6_q));  // open: D, Qn, preset, en, reset
  D_Flip_Flop d_ff_7 (.clk(and_8_out), .Q(d_ff_7_q));  // open: D, Qn, preset, en, reset
  D_Flip_Flop d_ff_8 (.clk(and_9_out), .Q(d_ff_8_q));  // open: D, Qn, preset, en, reset
  D_Flip_Flop Room_0 (.clk(and_10_out), .Q(Room_0_q));  // open: D, Qn, preset, en, reset
  not FREE9 (FREE9_out, Room_9_q);
  not not_1 (not_1_out, d_ff_1_q);
  not not_2 (not_2_out, d_ff_2_q);
  not not_3 (not_3_out, d_ff_3_q);
  not not_4 (not_4_out, d_ff_4_q);
  not not_5 (not_5_out, d_ff_5_q);
  not not_6 (not_6_out, d_ff_6_q);
  not not_7 (not_7_out, d_ff_7_q);
  not not_8 (not_8_out, d_ff_8_q);
  not FREE0 (FREE0_out, Room_0_q);
  or or_1 (or_1_out, not_1_out, or_2_out);
  or or_2 (or_2_out, not_2_out, or_3_out);
  or or_3 (or_3_out, not_3_out, or_4_out);
  or or_4 (or_4_out, not_4_out, or_5_out);
  or or_5 (or_5_out, not_5_out, or_6_out);
  or or_6 (or_6_out, not_6_out, or_7_out);
  or or_7 (or_7_out, not_7_out, or_8_out);
  or or_8 (or_8_out, not_8_out, FREE0_out);
  not not_9 (not_9_out, or_1_out);
  not not_10 (not_10_out, or_2_out);
  not not_11 (not_11_out, or_3_out);
  not not_12 (not_12_out, or_4_out);
  not not_13 (not_13_out, or_5_out);
  not not_14 (not_14_out, or_6_out);
  not not_15 (not_15_out, or_7_out);
  not not_16 (not_16_out, or_8_out);
  and ASSIGN9 (ASSIGN9_out, FREE9_out, REQ_out, not_9_out);
  and ASSIGN8 (ASSIGN8_out, not_1_out, REQ_out, not_10_out);
  and ASSIGN7 (ASSIGN7_out, not_2_out, REQ_out, not_11_out);
  and ASSIGN6 (ASSIGN6_out, not_3_out, REQ_out, not_12_out);
  and ASSIGN5 (ASSIGN5_out, not_4_out, REQ_out, not_13_out);
  and ASSIGN4 (ASSIGN4_out, not_5_out, REQ_out, not_14_out);
  and ASSIGN3 (ASSIGN3_out, not_6_out, REQ_out, not_15_out);
  and ASSIGN2 (ASSIGN2_out, not_7_out, REQ_out, not_16_out);
  and ASSIGN1 (ASSIGN1_out, not_8_out, REQ_out, Room_0_q);
  and ASSIGN0 (ASSIGN0_out, REQ_out, FREE0_out);
  D_Flip_Flop Retain_9 (
    .clk(ASSIGN9_out), .D(Retain_9_qn), .Q(Retain_9_q), .Qn(Retain_9_qn));  // open: preset, en, reset
  D_Flip_Flop d_ff_9 (.clk(ASSIGN8_out), .D(d_ff_9_qn), .Q(d_ff_9_q), .Qn(d_ff_9_qn));  // open: preset, en, reset
  D_Flip_Flop d_ff_10 (.clk(ASSIGN7_out), .D(d_ff_10_qn), .Q(d_ff_10_q), .Qn(d_ff_10_qn));  // open: preset, en, reset
  D_Flip_Flop d_ff_11 (.clk(ASSIGN6_out), .D(d_ff_11_qn), .Q(d_ff_11_q), .Qn(d_ff_11_qn));  // open: preset, en, reset
  D_Flip_Flop d_ff_12 (.clk(ASSIGN5_out), .D(d_ff_12_qn), .Q(d_ff_12_q), .Qn(d_ff_12_qn));  // open: preset, en, reset
  D_Flip_Flop d_ff_13 (.clk(ASSIGN4_out), .D(d_ff_13_qn), .Q(d_ff_13_q), .Qn(d_ff_13_qn));  // open: preset, en, reset
  D_Flip_Flop d_ff_14 (.clk(ASSIGN3_out), .D(d_ff_14_qn), .Q(d_ff_14_q), .Qn(d_ff_14_qn));  // open: preset, en, reset
  D_Flip_Flop d_ff_15 (.clk(ASSIGN2_out), .D(d_ff_15_qn), .Q(d_ff_15_q), .Qn(d_ff_15_qn));  // open: preset, en, reset
  D_Flip_Flop d_ff_16 (.clk(ASSIGN1_out), .D(d_ff_16_qn), .Q(d_ff_16_q), .Qn(d_ff_16_qn));  // open: preset, en, reset
  D_Flip_Flop Retain_0 (
    .clk(ASSIGN0_out), .D(Retain_0_qn), .Q(Retain_0_q), .Qn(Retain_0_qn));  // open: preset, en, reset
  LED led_1 (.in(Retain_9_q));
  LED led_2 (.in(d_ff_9_q));
  LED led_3 (.in(d_ff_10_q));
  LED led_4 (.in(d_ff_11_q));
  LED led_5 (.in(d_ff_12_q));
  LED led_6 (.in(d_ff_13_q));
  LED led_7 (.in(d_ff_14_q));
  LED led_8 (.in(d_ff_15_q));
  LED led_9 (.in(d_ff_16_q));
  LED led_10 (.in(Retain_0_q));
  or or_9 (or_9_out, Retain_9_q, d_ff_9_q, d_ff_10_q, d_ff_11_q, d_ff_12_q, d_ff_13_q, d_ff_14_q, d_ff_15_q, d_ff_16_q, Retain_0_q);
  not not_17 (not_17_out, or_9_out);
  LED led_11 (.in(not_17_out));
endmodule
